# Fritzing sketch circuit (saved by Fritzing 0.9.3b)
breadboards: 1

parts:
  Chirp!_Soil_Moisture_Sensor1 = Chirp! Soil Moisture Sensor v2.7.3
  Composant1 = Barometric Pressure Sensor - BMP180 Breakout (GY-68)
  M1 = DC Motor
  WeMos_D1_Mini_OLED_Shield1 = WeMos D1 Mini OLED Shield
  U2 = RELAY [package=relay-jzc]
  Mod1 = Raspberry Pi Pico

nets:
  N1: Chirp!_Soil_Moisture_Sensor1.Pin_0, Composant1.SCL, WeMos_D1_Mini_OLED_Shield1.5V, U2.COIL1
  N2: Chirp!_Soil_Moisture_Sensor1.pin_2, Composant1.SDA, M1.pin_2, WeMos_D1_Mini_OLED_Shield1.G, U2.NO
  N3: Chirp!_Soil_Moisture_Sensor1.pin_4, Mod1.pin_32
  N4: Composant1.VCC, Mod1.pin_4
  N5: Composant1.GND, Mod1.pin_5
  N6: M1.pin_1, U2.MAIN
  N7: WeMos_D1_Mini_OLED_Shield1.D3, Mod1.pin_2
  N8: WeMos_D1_Mini_OLED_Shield1.D4, Mod1.pin_1
  N9: U2.COIL2, Mod1.pin_3, Mod1.pin_8, Mod1.pin_13, Mod1.pin_18, Mod1.pin_23, Mod1.pin_28, Mod1.pin_33, Mod1.pin_38
  N10: U2.NC, Mod1.pin_40

custom parts:
  Raspberry Pi Pico: Raspberry Pi Pico. Based around the RP2040 microcontroller the Pico is a low cost microcontroller device bringing Raspberry Pi quality, cost, and easy of use to the microcontroller space. Jan 2021, Split part in to two versions: tht (this one) and SMD. This one will drill holes for a .1 in header in pcb to allow plugging in the module as well as providing pads to solder the module to the top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
